// Logisim project CPU_v24 bits.circ as structural Verilog: 2 circuits, main circuit main
module main (
  input  in_1
);

  wire adder_1_cout, and_1_out, and_2_out, and_3_out, and_5_out, and_6_out, clock_1_out, COMPOSITOR_carry,
       counter_2_carry, counter_3_carry, demultiplexer_1_out0, demultiplexer_1_out1, demultiplexer_1_out2,
       demultiplexer_1_out3, demultiplexer_1_out4, demultiplexer_1_out5, demultiplexer_1_out6,
       demultiplexer_1_out7, demultiplexer_1_out8, demultiplexer_1_out9, demultiplexer_1_out10,
       demultiplexer_1_out11, demultiplexer_1_out12, demultiplexer_1_out13, demultiplexer_1_out14,
       demultiplexer_1_out15, dualram_2_p2, GLOBAL_RESET_out, multiplexer_4_out, multiplexer_5_out,
       multiplexer_6_out, multiplexer_8_out, multiplexer_9_out, not_2_out, not_3_out, or_1_out, or_5_out,
       or_7_out, subtractor_1_bout, subtractor_3_bout, xnor_1_out, xor_1_out, xor_2_out, xor_3_out;
  wire [1:0] demultiplexer_4_out1_2, demultiplexer_4_out3_2, or_6_out;
  wire [2:0] CODE_ROM_data_4, CODE_ROM_data_7, counter_2_q, dualram_2_p3, subtractor_3_out;
  wire [3:0] BANK_q, bit_extender_6_out, FLAGS_q;
  wire [3:1] comparator_1_eq;
  wire [4:0] adder_5_out, COMPOSITOR_q, counter_2_q_2, counter_3_q, demultiplexer_3_out6,
       demultiplexer_3_out7, multiplexer_11_out, multiplexer_12_out, subtractor_4_out;
  wire [4:3] CODE_ROM_data_5;
  wire [5:0] adder_3_out, adder_4_out, bit_extender_1_out, bit_extender_2_out, bit_extender_3_out,
       bit_extender_7_out, PIXEL_OFFSET_q, shifter_4_out, subtractor_2_out;
  wire [5:3] CODE_ROM_data_8;
  wire [6:0] demultiplexer_4_out1, demultiplexer_4_out3;
  wire [7:0] A_out, multiplexer_14_out, RINPT_q, STACK_POINTER_q;
  wire [8:0] CODE_ROM_data_3, demultiplexer_4_out2, demultiplexer_4_out4;
  wire [11:0] dualram_1_p11, TILE_OFFSET_q;
  wire [11:10] multiplexer_10_out_2;
  wire [15:0] bit_extender_5_out, demultiplexer_5_out0, demultiplexer_5_out1, rom_1_data, shifter_3_out;
  wire [21:0] multiplexer_10_out;
  wire [23:0] adder_1_out, adder_2_out, and_4_out, bit_extender_4_out, CODE_ROM_data,
       controlled_buffer_1_out, controlled_buffer_2_out, controlled_buffer_3_out, controlled_buffer_4_out,
       counter_1_q, demultiplexer_2_out0, demultiplexer_2_out1, demultiplexer_2_out2, demultiplexer_2_out3,
       demultiplexer_2_out4, demultiplexer_2_out5, demultiplexer_2_out6, demultiplexer_2_out7,
       demultiplexer_3_out0, demultiplexer_3_out1, demultiplexer_3_out2, demultiplexer_3_out3,
       demultiplexer_3_out4, GEN_RAM_dout, multiplexer_1_out, multiplexer_2_out, multiplexer_3_out,
       multiplexer_7_out, not_1_out, or_4_out, R0_q, R1_q, R2_q, R3_q, R4_q, R5_q, R6_q, R7_q, R8_q, R9_q,
       R10_q, R11_q, R12_q, R13_q, R14_q, R15_q, shifter_1_out, shifter_2_out, STACK_dout, subtractor_1_out,
       xor_4_out;
  wire [23:5] demultiplexer_3_out6_2, demultiplexer_3_out7_2;
  wire [25:14] CODE_ROM_data_6;
  wire [31:24] CODE_ROM_data_2;
  wire [63:0] dualram_3_p35, multiplexer_13_out, RESOURCES_ROM_data, shifter_5_out, undriven;

  or or_1 (or_1_out, demultiplexer_4_out1[0], demultiplexer_4_out2[0]);
  Demultiplexer #(.select(4)) demultiplexer_1 (
    .out0(demultiplexer_1_out0), .out1(demultiplexer_1_out1), .out2(demultiplexer_1_out2),
    .out3(demultiplexer_1_out3), .out4(demultiplexer_1_out4), .out5(demultiplexer_1_out5),
    .out6(demultiplexer_1_out6), .out7(demultiplexer_1_out7), .out8(demultiplexer_1_out8),
    .out9(demultiplexer_1_out9), .out10(demultiplexer_1_out10), .out11(demultiplexer_1_out11),
    .out12(demultiplexer_1_out12), .out13(demultiplexer_1_out13), .out14(demultiplexer_1_out14),
    .out15(demultiplexer_1_out15), .in(or_1_out), .sel(CODE_ROM_data_6[25:22]));
  Clock clock_1 (.out(clock_1_out));
  Button GLOBAL_RESET (.out(GLOBAL_RESET_out));
  Register #(.width(24)) R0 (
    .D({multiplexer_10_out_2, multiplexer_10_out}), .en(demultiplexer_1_out0), .Q(R0_q), .clk(clock_1_out),
    .clr(GLOBAL_RESET_out));
  Register #(.width(24)) R4 (
    .D({multiplexer_10_out_2, multiplexer_10_out}), .en(demultiplexer_1_out4), .Q(R4_q), .clk(clock_1_out),
    .clr(GLOBAL_RESET_out));
  Register #(.width(24)) R8 (
    .D({multiplexer_10_out_2, multiplexer_10_out}), .en(demultiplexer_1_out8), .Q(R8_q), .clk(clock_1_out),
    .clr(GLOBAL_RESET_out));
  Register #(.width(24)) R12 (
    .D({multiplexer_10_out_2, multiplexer_10_out}), .en(demultiplexer_1_out12), .Q(R12_q), .clk(clock_1_out),
    .clr(GLOBAL_RESET_out));
  assign controlled_buffer_1_out = demultiplexer_4_out1[1] ? multiplexer_2_out : 24'bz;  // Controlled_Buffer controlled_buffer_1
  assign controlled_buffer_2_out = demultiplexer_4_out1[1] ? multiplexer_3_out : 24'bz;  // Controlled_Buffer controlled_buffer_2
  and and_1 (and_1_out, xor_1_out, xnor_1_out);
  Demultiplexer #(.select(3), .width(24)) demultiplexer_2 (
    .out0(demultiplexer_2_out0), .out1(demultiplexer_2_out1), .out2(demultiplexer_2_out2),
    .out3(demultiplexer_2_out3), .out4(demultiplexer_2_out4), .out5(demultiplexer_2_out5),
    .out6(demultiplexer_2_out6), .out7(demultiplexer_2_out7), .in(controlled_buffer_1_out),
    .sel(demultiplexer_4_out1[6:4]));
  Demultiplexer #(.select(3), .width(24)) demultiplexer_3 (
    .out0(demultiplexer_3_out0), .out1(demultiplexer_3_out1), .out2(demultiplexer_3_out2),
    .out3(demultiplexer_3_out3), .out4(demultiplexer_3_out4),
    .out6({demultiplexer_3_out6_2, demultiplexer_3_out6}),
    .out7({demultiplexer_3_out7_2, demultiplexer_3_out7}), .in(controlled_buffer_2_out),
    .sel(demultiplexer_4_out1[6:4]));  // open: out5
  Register #(.width(24)) R1 (
    .D({multiplexer_10_out_2, multiplexer_10_out}), .en(demultiplexer_1_out1), .Q(R1_q), .clk(clock_1_out),
    .clr(GLOBAL_RESET_out));
  Register #(.width(24)) R5 (
    .D({multiplexer_10_out_2, multiplexer_10_out}), .en(demultiplexer_1_out5), .Q(R5_q), .clk(clock_1_out),
    .clr(GLOBAL_RESET_out));
  Register #(.width(24)) R9 (
    .D({multiplexer_10_out_2, multiplexer_10_out}), .en(demultiplexer_1_out9), .Q(R9_q), .clk(clock_1_out),
    .clr(GLOBAL_RESET_out));
  Register #(.width(24)) R13 (
    .D({multiplexer_10_out_2, multiplexer_10_out}), .en(demultiplexer_1_out13), .Q(R13_q), .clk(clock_1_out),
    .clr(GLOBAL_RESET_out));
  xor xor_1 (xor_1_out, multiplexer_1_out[23], demultiplexer_2_out0[23]);
  xnor xnor_1 (xnor_1_out, demultiplexer_3_out0[23], demultiplexer_2_out0[23]);
  and and_2 (and_2_out, FLAGS_q[2], demultiplexer_4_out1[3]);
  Register #(.width(24)) R2 (
    .D({multiplexer_10_out_2, multiplexer_10_out}), .en(demultiplexer_1_out2), .Q(R2_q), .clk(clock_1_out),
    .clr(GLOBAL_RESET_out));
  Register #(.width(24)) R6 (
    .D({multiplexer_10_out_2, multiplexer_10_out}), .en(demultiplexer_1_out6), .Q(R6_q), .clk(clock_1_out),
    .clr(GLOBAL_RESET_out));
  Register #(.width(24)) R10 (
    .D({multiplexer_10_out_2, multiplexer_10_out}), .en(demultiplexer_1_out10), .Q(R10_q), .clk(clock_1_out),
    .clr(GLOBAL_RESET_out));
  Register #(.width(24)) R14 (
    .D({multiplexer_10_out_2, multiplexer_10_out}), .en(demultiplexer_1_out14), .Q(R14_q), .clk(clock_1_out),
    .clr(GLOBAL_RESET_out));
  or or_2 (comparator_1_eq[3], and_1_out, and_3_out);
  Register #(.width(24)) R3 (
    .D({multiplexer_10_out_2, multiplexer_10_out}), .en(demultiplexer_1_out3), .Q(R3_q), .clk(clock_1_out),
    .clr(GLOBAL_RESET_out));
  Register #(.width(24)) R7 (
    .D({multiplexer_10_out_2, multiplexer_10_out}), .en(demultiplexer_1_out7), .Q(R7_q), .clk(clock_1_out),
    .clr(GLOBAL_RESET_out));
  Register #(.width(24)) R11 (
    .D({multiplexer_10_out_2, multiplexer_10_out}), .en(demultiplexer_1_out11), .Q(R11_q), .clk(clock_1_out),
    .clr(GLOBAL_RESET_out));
  Register #(.width(24)) R15 (
    .D({multiplexer_10_out_2, multiplexer_10_out}), .en(demultiplexer_1_out15), .Q(R15_q), .clk(clock_1_out),
    .clr(GLOBAL_RESET_out));
  xor xor_2 (xor_2_out, multiplexer_1_out[23], demultiplexer_2_out1[23]);
  and and_3 (and_3_out, xor_2_out, xor_3_out);
  xor xor_3 (xor_3_out, demultiplexer_2_out1[23], demultiplexer_3_out1[23]);
  or or_3 (comparator_1_eq[2], adder_1_cout, subtractor_1_bout);
  Adder #(.width(24)) adder_1 (
    .a(demultiplexer_2_out0), .b(demultiplexer_3_out0), .out(adder_1_out), .cin(and_2_out),
    .cout(adder_1_cout));
  Subtractor #(.width(24)) subtractor_1 (
    .a(demultiplexer_2_out1), .b(demultiplexer_3_out1), .out(subtractor_1_out), .bin(and_2_out),
    .bout(subtractor_1_bout));
  assign and_4_out = demultiplexer_2_out2 & demultiplexer_3_out2;  // AND_Gate and_4, 24 bits wide
  assign or_4_out = demultiplexer_2_out3 | demultiplexer_3_out3;  // OR_Gate or_4, 24 bits wide
  assign xor_4_out = demultiplexer_2_out4 ^ demultiplexer_3_out4;  // XOR_Gate xor_4, 24 bits wide
  assign not_1_out = ~demultiplexer_2_out5;  // NOT_Gate not_1, 24 bits wide
  Shifter #(.width(24)) shifter_1 (.in(demultiplexer_2_out6), .\dist (demultiplexer_3_out6), .out(shifter_1_out));
  Shifter #(.shift("lr"), .width(24)) shifter_2 (
    .in(demultiplexer_2_out7), .\dist (demultiplexer_3_out7), .out(shifter_2_out));
  Comparator #(.mode("unsigned"), .width(24)) comparator_1 (
    .a(multiplexer_1_out), .b({24{1'b0}}), .eq(comparator_1_eq[1]));  // open: gt, lt
  Multiplexer #(.select(3), .width(24)) multiplexer_1 (
    .in0(adder_1_out), .in1(subtractor_1_out), .in2(and_4_out), .in3(or_4_out), .in4(xor_4_out),
    .in5(not_1_out), .in6(shifter_1_out), .in7(shifter_2_out), .out(multiplexer_1_out),
    .sel(demultiplexer_4_out1[6:4]));
  Register #(.width(4)) FLAGS (
    .D({comparator_1_eq, multiplexer_1_out[23]}), .en(demultiplexer_4_out1[2]), .Q(FLAGS_q),
    .clk(clock_1_out), .clr(GLOBAL_RESET_out));
  Multiplexer #(.select(4), .width(24)) multiplexer_2 (
    .in0(R0_q), .in1(R1_q), .in2(R2_q), .in3(R3_q), .in4(R4_q), .in5(R5_q), .in6(R6_q), .in7(R7_q),
    .in8(R8_q), .in9(R9_q), .in10(R10_q), .in11(R11_q), .in12(R12_q), .in13(R13_q), .in14(R14_q),
    .in15(R15_q), .out(multiplexer_2_out), .sel(CODE_ROM_data_6[17:14]));
  Multiplexer #(.select(4), .width(24)) multiplexer_3 (
    .in0(R0_q), .in1(R1_q), .in2(R2_q), .in3(R3_q), .in4(R4_q), .in5(R5_q), .in6(R6_q), .in7(R7_q),
    .in8(R8_q), .in9(R9_q), .in10(R10_q), .in11(R11_q), .in12(R12_q), .in13(R13_q), .in14(R14_q),
    .in15(R15_q), .out(multiplexer_3_out), .sel(CODE_ROM_data_6[21:18]));
  RAM #(.clearpin("true"), .dataWidth(24), .enables("line")) STACK (
    .addr(STACK_POINTER_q), .we(demultiplexer_4_out3[2]), .clk(clock_1_out), .din(adder_2_out),
    .dout(STACK_dout), .clr(GLOBAL_RESET_out));
  Counter STACK_POINTER (
    .count(demultiplexer_4_out3[4]), .Q(STACK_POINTER_q), .up(demultiplexer_4_out3[3]), .clk(clock_1_out),
    .clr(GLOBAL_RESET_out));  // open: load, D, carry
  Adder #(.width(24)) adder_2 (.a(24'h1), .b(counter_1_q), .out(adder_2_out));  // open: cin, cout
  Multiplexer #(.select(2)) multiplexer_4 (
    .in0(FLAGS_q[0]), .in1(FLAGS_q[1]), .in2(FLAGS_q[2]), .in3(FLAGS_q[3]), .out(multiplexer_4_out),
    .sel(demultiplexer_4_out3_2));
  Multiplexer multiplexer_5 (
    .in0(multiplexer_4_out), .in1(not_2_out), .out(multiplexer_5_out), .sel(demultiplexer_4_out3[6]));
  not not_2 (not_2_out, multiplexer_6_out);
  Multiplexer #(.select(2)) multiplexer_6 (
    .in0(FLAGS_q[0]), .in1(FLAGS_q[1]), .in2(FLAGS_q[2]), .in3(FLAGS_q[3]), .out(multiplexer_6_out),
    .sel(demultiplexer_4_out3_2));
  RAM #(.addrWidth(24), .clearpin("true"), .dataWidth(24), .enables("line")) GEN_RAM (
    .addr(controlled_buffer_3_out), .we(demultiplexer_4_out2[1]), .clk(clock_1_out),
    .din(controlled_buffer_4_out), .dout(GEN_RAM_dout), .clr(GLOBAL_RESET_out));
  assign controlled_buffer_3_out = demultiplexer_4_out2[2] ? multiplexer_2_out : 24'bz;  // Controlled_Buffer controlled_buffer_3
  assign controlled_buffer_4_out = demultiplexer_4_out2[2] ? {multiplexer_10_out_2, multiplexer_10_out} : 24'bz;  // Controlled_Buffer controlled_buffer_4
  and and_5 (and_5_out, demultiplexer_4_out3[5], multiplexer_5_out);
  Demultiplexer #(.select(3), .width(9)) demultiplexer_4 (
    .out1({demultiplexer_4_out1_2, demultiplexer_4_out1}), .out2(demultiplexer_4_out2),
    .out3({demultiplexer_4_out3_2, demultiplexer_4_out3}), .out4(demultiplexer_4_out4), .in(CODE_ROM_data_3),
    .sel(CODE_ROM_data_7));  // open: out0, out5, out6, out7
  or or_5 (or_5_out, demultiplexer_4_out3[0], and_5_out);
  Multiplexer #(.width(24)) multiplexer_7 (
    .in0(CODE_ROM_data), .in1(STACK_dout), .out(multiplexer_7_out), .sel(demultiplexer_4_out3[1]));
  Counter #(.max('hffffff), .width(24)) counter_1 (
    .load(or_5_out), .D(multiplexer_7_out), .count(multiplexer_8_out), .Q(counter_1_q), .up(1'b1),
    .clk(clock_1_out), .clr(GLOBAL_RESET_out));  // open: carry
  Multiplexer multiplexer_8 (
    .in0(1'b1), .in1(multiplexer_9_out), .out(multiplexer_8_out), .sel(demultiplexer_4_out4[0]));
  Multiplexer multiplexer_9 (
    .in0(counter_2_carry), .in1(and_6_out), .out(multiplexer_9_out), .sel(demultiplexer_4_out4[1]));
  Multiplexer #(.select(3), .width(24)) multiplexer_10 (
    .in0(multiplexer_1_out), .in1(multiplexer_3_out), .in2(GEN_RAM_dout), .in3(CODE_ROM_data),
    .in4(bit_extender_4_out), .out({multiplexer_10_out_2, multiplexer_10_out}), .sel(CODE_ROM_data_4));  // open: in5, in6, in7
  ROM #(.addrWidth(24), .dataWidth(64)) CODE_ROM (
    .addr(counter_1_q),
    .data({CODE_ROM_data_8, CODE_ROM_data_7, CODE_ROM_data_6, CODE_ROM_data_5, CODE_ROM_data_4, CODE_ROM_data_3, CODE_ROM_data_2, CODE_ROM_data}));
  assign or_6_out = demultiplexer_4_out1_2 | demultiplexer_4_out2[4:3];  // OR_Gate or_6, 2 bits wide
  Register RINPT (.D(A_out), .en(1'b1), .Q(RINPT_q), .clk(clock_1_out), .clr(GLOBAL_RESET_out));
  Button LEFT (.out(A_out[5]));
  Register #(.width(12)) TILE_OFFSET (
    .D({multiplexer_10_out[17:12], multiplexer_10_out[8:3]}), .en(or_6_out[0]), .Q(TILE_OFFSET_q),
    .clk(clock_1_out), .clr(GLOBAL_RESET_out));
  assign bit_extender_1_out = {{1{1'b0}}, COMPOSITOR_q};  // Bit_Extender bit_extender_1
  assign bit_extender_2_out = {{1{1'b0}}, counter_3_q};  // Bit_Extender bit_extender_2
  assign bit_extender_3_out = {{5{1'b0}}, subtractor_3_bout};  // Bit_Extender bit_extender_3
  assign bit_extender_4_out = {{16{1'b0}}, RINPT_q};  // Bit_Extender bit_extender_4
  Button UP (.out(A_out[4]));
  Button DOWN (.out(A_out[7]));
  Adder #(.width(6)) adder_3 (.a(TILE_OFFSET_q[5:0]), .b(bit_extender_1_out), .out(adder_3_out));  // open: cin, cout
  Adder #(.width(6)) adder_4 (.a(TILE_OFFSET_q[11:6]), .b(bit_extender_2_out), .out(adder_4_out));  // open: cin, cout
  Subtractor #(.width(6)) subtractor_2 (
    .a(adder_4_out), .b(bit_extender_3_out), .out(subtractor_2_out));  // open: bin, bout
  Button B (.out(A_out[1]));
  Button RIGHT (.out(A_out[6]));
  Button Y (.out(A_out[3]));
  Button X (.out(A_out[2]));
  Button A (.out(A_out[0]));
  Register #(.width(6)) PIXEL_OFFSET (
    .D({multiplexer_10_out[11:9], multiplexer_10_out[2:0]}), .en(or_6_out[0]), .Q(PIXEL_OFFSET_q),
    .clk(clock_1_out), .clr(GLOBAL_RESET_out));
  // DualRAM #(.addrWidth(12), .dataWidth(12), .trigger("falling")) dualram_1: pin names not known; wires that end beside it: {subtractor_2_out, adder_3_out}, 1'b0, 1'b1, clock_1_out, multiplexer_10_out[11:0], or_6_out[1], 1'b0, clock_1_out, {multiplexer_10_out_2, multiplexer_10_out[21:12]}, GLOBAL_RESET_out, dualram_1_p11
  Register #(.width(4)) BANK (
    .D(multiplexer_10_out[21:18]), .en(or_6_out[0]), .Q(BANK_q), .clk(clock_1_out), .clr(GLOBAL_RESET_out));
  Subtractor #(.width(3)) subtractor_3 (
    .a(dualram_2_p3), .b(PIXEL_OFFSET_q[5:3]), .out(subtractor_3_out), .bout(subtractor_3_bout));  // open: bin
  ROM #(.addrWidth(20), .dataWidth(64)) RESOURCES_ROM (
    .addr({in_1, BANK_q, dualram_1_p11, subtractor_3_out}), .data(RESOURCES_ROM_data));
  or or_7 (or_7_out, counter_2_carry, not_3_out);
  assign bit_extender_5_out = {{8{1'b0}}, {8{1'b1}}};  // Bit_Extender bit_extender_5
  assign bit_extender_6_out = {{1{1'b0}}, PIXEL_OFFSET_q[2:0]};  // Bit_Extender bit_extender_6
  assign bit_extender_7_out = {{3{1'b0}}, PIXEL_OFFSET_q[2:0]};  // Bit_Extender bit_extender_7
  not not_3 (not_3_out, COMPOSITOR_carry);
  Counter #(.max('h1f), .width(5)) COMPOSITOR (
    .count(or_7_out), .Q(COMPOSITOR_q), .carry(COMPOSITOR_carry), .clk(clock_1_out), .clr(GLOBAL_RESET_out));  // open: load, D, up
  Demultiplexer #(.width(16)) demultiplexer_5 (
    .out0(demultiplexer_5_out0), .out1(demultiplexer_5_out1), .in(shifter_3_out), .sel(dualram_2_p3[0]));
  Shifter #(.shift("rr"), .width(16)) shifter_3 (
    .in(bit_extender_5_out), .\dist (bit_extender_6_out), .out(shifter_3_out));
  Shifter #(.width(6)) shifter_4 (.in(bit_extender_7_out), .\dist (3'b011), .out(shifter_4_out));
  Multiplexer #(.width(5)) multiplexer_11 (
    .in0(COMPOSITOR_q), .in1(adder_5_out), .out(multiplexer_11_out), .sel(dualram_2_p3[0]));
  Subtractor #(.width(5)) subtractor_4 (.a(COMPOSITOR_q), .b(5'b00001), .out(subtractor_4_out));  // open: bin, bout
  Shifter #(.shift("rl"), .width(64)) shifter_5 (.in(RESOURCES_ROM_data), .\dist (shifter_4_out), .out(shifter_5_out));
  Multiplexer #(.width(5)) multiplexer_12 (
    .in0(COMPOSITOR_q), .in1(adder_5_out), .out(multiplexer_12_out), .sel(dualram_2_p2));
  // DualRAM #(.addrWidth(5), .byteenables("byteEnables"), .dataWidth(64), .trigger("falling")) dualram_2: pin names not known; wires that end beside it: multiplexer_11_out, dualram_2_p2, dualram_2_p3[0], clock_1_out, demultiplexer_5_out0[0], demultiplexer_5_out0[1], demultiplexer_5_out0[2], demultiplexer_5_out0[3], demultiplexer_5_out0[4], demultiplexer_5_out0[5], demultiplexer_5_out0[6], demultiplexer_5_out0[7], shifter_5_out
  not not_4 (dualram_2_p2, dualram_2_p3[0]);
  // DualRAM #(.addrWidth(5), .byteenables("byteEnables"), .dataWidth(64), .trigger("falling")) dualram_3: pin names not known; wires that end beside it: subtractor_4_out, dualram_2_p2, dualram_2_p3[0], clock_1_out, demultiplexer_5_out0[8], demultiplexer_5_out0[9], demultiplexer_5_out0[10], demultiplexer_5_out0[11], demultiplexer_5_out0[12], demultiplexer_5_out0[13], demultiplexer_5_out0[14], demultiplexer_5_out0[15], shifter_5_out, multiplexer_12_out, dualram_2_p3[0], dualram_2_p2, clock_1_out, demultiplexer_5_out1[0], demultiplexer_5_out1[1], demultiplexer_5_out1[2], demultiplexer_5_out1[3], demultiplexer_5_out1[4], demultiplexer_5_out1[5], demultiplexer_5_out1[6], demultiplexer_5_out1[7], shifter_5_out, subtractor_4_out, dualram_2_p3[0], dualram_2_p2, clock_1_out, demultiplexer_5_out1[8], demultiplexer_5_out1[9], demultiplexer_5_out1[10], demultiplexer_5_out1[11], dualram_3_p35
  Adder #(.width(5)) adder_5 (.a(5'b00001), .b(counter_2_q_2), .out(adder_5_out));  // open: cin, cout
  Multiplexer #(.width(64)) multiplexer_13 (
    .in0(undriven), .in1(dualram_3_p35), .out(multiplexer_13_out), .sel(dualram_2_p2));
  ROM #(.dataWidth(16)) rom_1 (.addr(multiplexer_14_out), .data(rom_1_data));
  Multiplexer #(.select(3), .width(8)) multiplexer_14 (
    .in0(multiplexer_13_out[63:56]), .in1(multiplexer_13_out[55:48]), .in2(multiplexer_13_out[47:40]),
    .in3(multiplexer_13_out[39:32]), .in4(multiplexer_13_out[31:24]), .in5(multiplexer_13_out[23:16]),
    .in6(multiplexer_13_out[15:8]), .in7(multiplexer_13_out[7:0]), .out(multiplexer_14_out), .sel(counter_2_q));
  Counter counter_2 (
    .Q({counter_2_q_2, counter_2_q}), .carry(counter_2_carry), .up(1'b1), .clk(clock_1_out),
    .clr(GLOBAL_RESET_out));  // open: load, D, count
  Counter counter_3 (
    .count(counter_2_carry), .Q({counter_3_q, dualram_2_p3}), .carry(counter_3_carry), .up(1'b1),
    .clk(clock_1_out), .clr(GLOBAL_RESET_out));  // open: load, D
  // RGB_Video #(.height(256), .scale(1), .width(256)) rgb_video_1: pin names not known; wires that end beside it: GLOBAL_RESET_out, clock_1_out, 1'b1, {counter_2_q_2, counter_2_q}, {counter_3_q, dualram_2_p3}, rom_1_data
  and and_6 (and_6_out, counter_3_carry, counter_2_carry);

  // Notes on the sheet:
  //   BUS_C
  //   BUS_A
  //   REGS_CONTROL
  //   BUS B
  //   ALU_CONTROL
  //   PC_CONTROL
  //   BUS B
  //   STOP_CONTROL
  //   ALU_CONTROL
  //   MOV_CONTROL
  //   BUS_C
  //   ALU_OUT
  //   contents of CODE_ROM (hex, n*v repeats v):
  //   800061000008000 80006100000f001 80006100000c002 800061000001003 800061000000004 80006100000d005
  //   800061000015006 80006100000e007 800061000004008 80006100000f009 800060100000001 88006010000007f
  //   840060100000000 1000000300000000 440408300000000 408401600000000 c0000a00000000c c0000010000000d
  //   FINE_CONTROL
  //   BUS_C_SEL
  //   REGS_CONTROL
  //   OPCODE
  //   contents of RESOURCES_ROM (hex, n*v repeats v):
  //   9*0 c0c0c0c0000 c000000000c00 c000000000c00 c000000000c00 c0c0c0c0c0c00 c000000000c00 c000000000c00
  //   0 c0c0c0c0c0000 c000000000c00 c000000000c00 c0c0c0c0c0000 c000000000c00 c000000000c00 c0c0c0c0c0000
  //   0 c0c0c0c0000 c000000000c00 c000000000000 c000000000000 c000000000000 c000000000c00 c0c0c0c0000 0
  //   c0c0c0c0c0000 5*c000000000c00 c0c0c0c0c0000 0 c0c0c0c0c0000 c000000000000 c000000000000
  //   c0c0c0c0c0000 c000000000000 c000000000000 c0c0c0c0c0000 0 c0c0c0c0c0000 c000000000000 c000000000000
  //   c0c0c0c000000 c000000000000 c000000000000 c000000000000 0 c0c0c000000 c0000000c0000 c000000000000
  //   c000c0c0c0000 c0000000c0000 c0000000c0000 c0c0c000000 0 c0000000c0000 c0000000c0000 c0000000c0000
  //   c0c0c0c0c0000 c0000000c0000 c0000000c0000 c0000000c0000 0 c0c0c0c0c0000 5*c00000000 c0c0c0c0c0000 0
  //   c0c0c0c0c0000 4*c0000 c0000000c0000 c0c0c000000 0 c0000000c0000 c00000c000000 c000c00000000
  //   c0c0000000000 c000c00000000 c00000c000000 c0000000c0000 0 6*c000000000000 c0c0c0c0c0000 0
  //   c0000000c0000 c0c000c0c0000 c000c000c0000 4*c0000000c0000 0 c0000000c0000 c0c00000c0000
  //   c0c00000c0000 c000c000c0000 c000c000c0000 c00000c0c0000 c00000c0c0000 0 c0c0c000000 5*c0000000c0000
  //   c0c0c000000 0 c0c0c0c000000 c0000000c0000 c0000000c0000 c0000000c0000 c0c0c0c000000 c000000000000
  //   c000000000000 0 c0c0c000000 4*c0000000c0000 c00000c0c0000 c0c0c0c0c00 0 c0c0c0c000000 c0000000c0000
  //   c0000000c0000 c0c0c0c000000 c0000000c0000 c0000000c0000 c0000000c0000 0 c0c0c000000 c0000000c0000
  //   c000000000000 c0c0c000000 c0000 c0000000c0000 c0c0c000000 0 c0c0c0c0c0000 6*c00000000 0
  //   6*c0000000c0000 c0c0c000000 0 4*c0000000c0000 c000c000000 c000c000000 c00000000 0 6*c000c000c0000
  //   c000c000000 0 c0000000c0000 c0000000c0000 c000c000000 c00000000 c000c000000 c0000000c0000
  //   c0000000c0000 0 c0000000c0000 c0000000c0000 c0000000c0000 c000c000000 c00000000 c00000000 c00000000
  //   0 c0c0c0c0c0000 c0000 c000000 c00000000 c0000000000 c000000000000 c0c0c0c0c0000 8*c0c0c0c0c0c0c0c
  //   8*1020304050607
  //   contents of rom_1 (hex, n*v repeats v):
  //   18e5 592b b1ea ebea fe6e a78e 3dac 238f 29ad 3af9 453e 777e f7be 9598 5370 31ea
endmodule

module gpu (
  input  [4:0] in_1,
  input  in_2,
  input  [2:0] in_3
);

  wire dualram_1_p4, not_1_out;
  wire [3:0] bit_extender_2_out;
  wire [4:0] multiplexer_1_out, multiplexer_2_out, multiplexer_3_out, multiplexer_4_out, subtractor_1_out;
  wire [5:0] bit_extender_3_out, shifter_2_out;
  wire [15:0] bit_extender_1_out, demultiplexer_1_out0, demultiplexer_1_out1, shifter_1_out;
  wire [63:0] dualram_1_p14, dualram_2_p35, shifter_3_out;

  assign bit_extender_1_out = {{8{1'b0}}, {8{1'b1}}};  // Bit_Extender bit_extender_1
  assign bit_extender_2_out = {{1{1'b0}}, in_3};  // Bit_Extender bit_extender_2
  assign bit_extender_3_out = {{3{1'b0}}, in_3};  // Bit_Extender bit_extender_3
  Demultiplexer #(.width(16)) demultiplexer_1 (
    .out0(demultiplexer_1_out0), .out1(demultiplexer_1_out1), .in(shifter_1_out), .sel(in_2));
  Shifter #(.width(16)) shifter_1 (.in(bit_extender_1_out), .\dist (bit_extender_2_out), .out(shifter_1_out));
  Shifter #(.width(6)) shifter_2 (.in(bit_extender_3_out), .\dist (3'b011), .out(shifter_2_out));
  Shifter #(.shift("rl"), .width(64)) shifter_3 (
    .in(64'h1122334455667788), .\dist (shifter_2_out), .out(shifter_3_out));
  Multiplexer #(.width(5)) multiplexer_1 (.in0(in_1), .out(multiplexer_1_out), .sel(in_2));  // open: in1
  Subtractor #(.width(5)) subtractor_1 (.a(in_1), .b(5'b00001), .out(subtractor_1_out));  // open: bin, bout
  Multiplexer #(.width(5)) multiplexer_2 (.in0(subtractor_1_out), .out(multiplexer_2_out), .sel(in_2));  // open: in1
  Multiplexer #(.width(5)) multiplexer_3 (.in0(in_1), .out(multiplexer_3_out), .sel(not_1_out));  // open: in1
  Multiplexer #(.width(5)) multiplexer_4 (
    .in0(subtractor_1_out), .out(multiplexer_4_out), .sel(not_1_out));  // open: in1
  not not_1 (not_1_out, in_2);
  // DualRAM #(.addrWidth(5), .byteenables("byteEnables"), .dataWidth(64), .trigger("falling")) dualram_1: pin names not known; wires that end beside it: multiplexer_1_out, not_1_out, in_2, dualram_1_p4, demultiplexer_1_out0[0], demultiplexer_1_out0[1], demultiplexer_1_out0[2], demultiplexer_1_out0[3], demultiplexer_1_out0[4], demultiplexer_1_out0[5], demultiplexer_1_out0[6], demultiplexer_1_out0[7], shifter_3_out, dualram_1_p14
  // DualRAM #(.addrWidth(5), .byteenables("byteEnables"), .dataWidth(64), .trigger("falling")) dualram_2: pin names not known; wires that end beside it: multiplexer_2_out, not_1_out, in_2, dualram_1_p4, demultiplexer_1_out0[8], demultiplexer_1_out0[9], demultiplexer_1_out0[10], demultiplexer_1_out0[11], demultiplexer_1_out0[12], demultiplexer_1_out0[13], demultiplexer_1_out0[14], demultiplexer_1_out0[15], shifter_3_out, multiplexer_3_out, in_2, not_1_out, dualram_1_p4, demultiplexer_1_out1[0], demultiplexer_1_out1[1], demultiplexer_1_out1[2], demultiplexer_1_out1[3], demultiplexer_1_out1[4], demultiplexer_1_out1[5], demultiplexer_1_out1[6], demultiplexer_1_out1[7], shifter_3_out, multiplexer_4_out, in_2, not_1_out, dualram_1_p4, demultiplexer_1_out1[8], demultiplexer_1_out1[9], demultiplexer_1_out1[10], demultiplexer_1_out1[11], dualram_2_p35
  Multiplexer #(.width(64)) multiplexer_5 (.in0(dualram_1_p14), .in1(dualram_2_p35), .sel(not_1_out));  // open: out
endmodule
